# Fritzing sketch Control (saved by Fritzing 0.9.3b)
breadboards: 1

parts:
  Raspberry_Pi_1 = Raspberry Pi 3 [part_number=RPI-3-V1.2]
  U2 = Voltage Regulator [package=to220-adj]
  R2 = Resistor [tolerance=±5% resistance=1.2k package="0805 [SMD]"]
  S1 = Momentary Switch [package=ksa_sealed_tac_switch]
  R1 = Resistor [tolerance=±5% resistance=1.2k package="0805 [SMD]"]
  R3 = Resistor [tolerance=±5% resistance=1.2k package="0805 [SMD]"]
  U3 = RELAY [package=relay-jzc]
  S2 = Momentary Switch [package=ksa_sealed_tac_switch]
  S3 = Momentary Switch [package=ksa_sealed_tac_switch]
  S4 = Momentary Switch [package=ksa_sealed_tac_switch]
  R4 = Resistor [tolerance=±5% resistance=1.2k package="0805 [SMD]"]
  VCC1 = 4 x AAA Battery Mount
  R5 = Resistor [tolerance=±5% resistance=1.2k package="0805 [SMD]"]
  R6 = Resistor [tolerance=±5% resistance=1.2k package="0805 [SMD]"]

nets:
  N1: Raspberry_Pi_1.GND, R2.Pin_1, U3.COIL2, VCC1.-
  N2: Raspberry_Pi_1.GIPO17, S2.2
  N3: Raspberry_Pi_1.GIPO27, S4.2
  N4: Raspberry_Pi_1.GIPO22, U3.NC
  N5: Raspberry_Pi_1.GIPO24, S3.2
  N6: U2.ADJ, R2.Pin_0, R1.Pin_1
  N7: U2.IN, R1.Pin_0, R3.Pin_1, R4.Pin_1, R5.Pin_1, R6.Pin_1
  N8: U2.OUT, U3.NO, VCC1.+
  N9: S1.4, R4.Pin_0
  N10: R3.Pin_0, S3.4
  N11: S2.4, R5.Pin_0
  N12: S4.4, R6.Pin_0
