# Fritzing sketch Switch-Led (saved by Fritzing 0.9.3b)
breadboards: 1

parts:
  Raspberry_Pi_1 = Raspberry Pi 3 [part_number=RPI-3-V1.2]
  R1 = Resistor [tolerance=±5% resistance=220 package="2010 [SMD]"]
  R2 = Resistor [tolerance=±5% resistance=220 package="2010 [SMD]"]
  LED1 = LED - 3mm [color="Blue (430nm)" package="3 mm [THT]"]
  S1 = Momentary Switch [package=ksa_sealed_tac_switch]

nets:
  N1: Raspberry_Pi_1.GND, LED1.cathode
  N2: Raspberry_Pi_1.GIPO17, S1.4
  N3: Raspberry_Pi_1.GIPO27, R1.Pin_1
  N4: Raspberry_Pi_1.GIPO6, R2.Pin_1
  N5: R1.Pin_0, LED1.anode
  N6: R2.Pin_0, S1.2
